# Fritzing sketch globe_board (saved by Fritzing 0.7.10b)
stripboards: 1

parts:
  U1 = atmega168 [package=dip]
  LED1 = LED - 5mm [color="Infrared (940nm)" package="5 mm [THT]"]
  R1 = Resistor [tolerance=±5% resistance=100 package=THT]
  J4 = female alternating pin header, 2 pins [form="♀ (female)"]

nets:
  N1: U1.D2, LED1.anode, J4.pin2
  N2: U1.GND#7, R1.Pin_0
  N3: LED1.cathode, R1.Pin_1, J4.pin1
